// Digital circuit 4 bit adder.dig as structural Verilog
module _4_bit_adder (
  input  [3:0] A,
  input  [3:0] B,
  input  Carry_in,
  output [3:0] Sum
);

  wire one_bit_full_adder_2_carry, one_bit_full_adder_3_carry, one_bit_full_adder_4_carry;

  one_bit_full_adder one_bit_full_adder_1 (
    .A(A[3]), .B(B[3]), .C(one_bit_full_adder_2_carry), .Sum(Sum[3]));  // open: Carry
  one_bit_full_adder one_bit_full_adder_2 (
    .A(A[2]), .B(B[2]), .C(one_bit_full_adder_3_carry), .Sum(Sum[2]), .Carry(one_bit_full_adder_2_carry));
  one_bit_full_adder one_bit_full_adder_3 (
    .A(A[1]), .B(B[1]), .C(one_bit_full_adder_4_carry), .Sum(Sum[1]), .Carry(one_bit_full_adder_3_carry));
  one_bit_full_adder one_bit_full_adder_4 (
    .A(A[0]), .B(B[0]), .C(Carry_in), .Sum(Sum[0]), .Carry(one_bit_full_adder_4_carry));
endmodule
