// Digital circuit Control_RType_v3.dig as structural Verilog
module Control_RType_v3 (
  input  clk,
  output [4:0] states,
  output IR_HI_Write,
  output IR_LO_Write,
  output Increment_PC,
  output WriteBack
);

  D_FF #(.Default(1)) IF1 (.D(states[4]), .C(clk), .Q(IR_HI_Write));  // open: nQ
  D_FF IF2 (.D(IR_HI_Write), .C(clk), .Q(IR_LO_Write));  // open: nQ
  D_FF Decode (.D(IR_LO_Write), .C(clk), .Q(states[2]));  // open: nQ
  D_FF Execute (.D(states[2]), .C(clk), .Q(states[3]));  // open: nQ
  or or_1 (Increment_PC, IR_HI_Write, states[4]);
  D_FF u_WriteBack (.D(states[3]), .C(clk), .Q(states[4]));  // open: nQ

  assign states[1:0] = {IR_LO_Write, IR_HI_Write};
  assign WriteBack = states[4];
endmodule
