// Digital circuit DRAM1.dig as structural Verilog
module DRAM1 (
  input  [3:0] adress_bits,
  input  Clk,
  input  [1:0] Store_Clear_Load,
  input  [3:0] Data_Input,
  output [3:0] Data_Output
);

  wire and_1_out, and_2_out, and_3_out, and_4_out, and_5_out, and_6_out, and_7_out, and_8_out, and_9_out,
       and_10_out, and_11_out, and_12_out, and_13_out, and_14_out, and_15_out, and_16_out, decoder_1_out_0,
       decoder_1_out_1, decoder_1_out_2, decoder_1_out_3, decoder_1_out_4, decoder_1_out_5, decoder_1_out_6,
       decoder_1_out_7, decoder_1_out_8, decoder_1_out_9, decoder_1_out_10, decoder_1_out_11,
       decoder_1_out_12, decoder_1_out_13, decoder_1_out_14, decoder_1_out_15;
  wire [3:0] Row_0_output, Row_1_output, Row_2_output, Row_3_output, Row_4_output, Row_5_output,
       Row_6_output, Row_7_output, Row_8_output, Row_9_output, Row_10_output, Row_11_output, Row_12_output,
       Row_13_output, Row_14_output, storeclearloadcircuit_1_output;

  Decoder #(.Selector_Bits(4)) decoder_1 (
    .sel(adress_bits), .out_0(decoder_1_out_0), .out_1(decoder_1_out_1), .out_2(decoder_1_out_2),
    .out_3(decoder_1_out_3), .out_4(decoder_1_out_4), .out_5(decoder_1_out_5), .out_6(decoder_1_out_6),
    .out_7(decoder_1_out_7), .out_8(decoder_1_out_8), .out_9(decoder_1_out_9), .out_10(decoder_1_out_10),
    .out_11(decoder_1_out_11), .out_12(decoder_1_out_12), .out_13(decoder_1_out_13),
    .out_14(decoder_1_out_14), .out_15(decoder_1_out_15));
  and and_1 (and_1_out, decoder_1_out_0, Clk);
  and and_2 (and_2_out, decoder_1_out_4, Clk);
  and and_3 (and_3_out, decoder_1_out_8, Clk);
  and and_4 (and_4_out, decoder_1_out_12, Clk);
  storeclearloadcircuit Row_0 (
    .\input (Data_Input), .clk(and_1_out), .store_clear_load(Store_Clear_Load), .Output(Row_0_output));
  storeclearloadcircuit Row_4 (
    .\input (Data_Input), .clk(and_2_out), .store_clear_load(Store_Clear_Load), .Output(Row_4_output));
  storeclearloadcircuit Row_8 (
    .\input (Data_Input), .clk(and_3_out), .store_clear_load(Store_Clear_Load), .Output(Row_8_output));
  storeclearloadcircuit Row_12 (
    .\input (Data_Input), .clk(and_4_out), .store_clear_load(Store_Clear_Load), .Output(Row_12_output));
  and and_5 (and_5_out, decoder_1_out_1, Clk);
  and and_6 (and_6_out, decoder_1_out_5, Clk);
  and and_7 (and_7_out, decoder_1_out_9, Clk);
  and and_8 (and_8_out, decoder_1_out_13, Clk);
  storeclearloadcircuit Row_1 (
    .\input (Data_Input), .clk(and_5_out), .store_clear_load(Store_Clear_Load), .Output(Row_1_output));
  storeclearloadcircuit Row_5 (
    .\input (Data_Input), .clk(and_6_out), .store_clear_load(Store_Clear_Load), .Output(Row_5_output));
  storeclearloadcircuit Row_9 (
    .\input (Data_Input), .clk(and_7_out), .store_clear_load(Store_Clear_Load), .Output(Row_9_output));
  storeclearloadcircuit Row_13 (
    .\input (Data_Input), .clk(and_8_out), .store_clear_load(Store_Clear_Load), .Output(Row_13_output));
  and and_9 (and_9_out, decoder_1_out_2, Clk);
  and and_10 (and_10_out, decoder_1_out_6, Clk);
  and and_11 (and_11_out, decoder_1_out_10, Clk);
  and and_12 (and_12_out, decoder_1_out_14, Clk);
  storeclearloadcircuit Row_2 (
    .\input (Data_Input), .clk(and_9_out), .store_clear_load(Store_Clear_Load), .Output(Row_2_output));
  storeclearloadcircuit Row_6 (
    .\input (Data_Input), .clk(and_10_out), .store_clear_load(Store_Clear_Load), .Output(Row_6_output));
  storeclearloadcircuit Row_10 (
    .\input (Data_Input), .clk(and_11_out), .store_clear_load(Store_Clear_Load), .Output(Row_10_output));
  storeclearloadcircuit Row_14 (
    .\input (Data_Input), .clk(and_12_out), .store_clear_load(Store_Clear_Load), .Output(Row_14_output));
  and and_13 (and_13_out, decoder_1_out_3, Clk);
  and and_14 (and_14_out, decoder_1_out_7, Clk);
  and and_15 (and_15_out, decoder_1_out_11, Clk);
  and and_16 (and_16_out, decoder_1_out_15, Clk);
  storeclearloadcircuit Row_3 (
    .\input (Data_Input), .clk(and_13_out), .store_clear_load(Store_Clear_Load), .Output(Row_3_output));
  storeclearloadcircuit Row_7 (
    .\input (Data_Input), .clk(and_14_out), .store_clear_load(Store_Clear_Load), .Output(Row_7_output));
  storeclearloadcircuit Row_11 (
    .\input (Data_Input), .clk(and_15_out), .store_clear_load(Store_Clear_Load), .Output(Row_11_output));
  storeclearloadcircuit storeclearloadcircuit_1 (
    .\input (Data_Input), .clk(and_16_out), .store_clear_load(Store_Clear_Load),
    .Output(storeclearloadcircuit_1_output));
  Multiplexer #(.Bits(4), .Selector_Bits(4)) multiplexer_1 (
    .sel(adress_bits), .in_0(Row_0_output), .in_1(Row_1_output), .in_2(Row_2_output), .in_3(Row_3_output),
    .in_4(Row_4_output), .in_5(Row_5_output), .in_6(Row_6_output), .in_7(Row_7_output), .in_8(Row_8_output),
    .in_9(Row_9_output), .in_10(Row_10_output), .in_11(Row_11_output), .in_12(Row_12_output),
    .in_13(Row_13_output), .in_14(Row_14_output), .in_15(storeclearloadcircuit_1_output), .out(Data_Output));
endmodule
