// Digital circuit RegisterFiles.dig as structural Verilog
module RegisterFiles (
  input  CLK,
  input  [1:0] ReadRegister_1,
  input  [1:0] ReadRegister_2,
  input  [7:0] Control_signals,
  input  [3:0] Write_data,
  input  [1:0] WriteRegister,
  output [3:0] ReadData_1,
  output [3:0] ReadData_2
);

  wire [3:0] demultiplexer_1_out_0, demultiplexer_1_out_1, demultiplexer_1_out_2, demultiplexer_1_out_3,
       R0_output, R1_output, R2_output, R3_output;

  Demultiplexer #(.Bits(4), .Selector_Bits(2)) demultiplexer_1 (
    .sel(WriteRegister), .in(Write_data), .out_0(demultiplexer_1_out_0), .out_1(demultiplexer_1_out_1),
    .out_2(demultiplexer_1_out_2), .out_3(demultiplexer_1_out_3));
  storeclearloadcircuit R0 (
    .\input (demultiplexer_1_out_0), .clk(CLK), .store_clear_load(Control_signals[1:0]), .Output(R0_output));
  storeclearloadcircuit R1 (
    .\input (demultiplexer_1_out_1), .clk(CLK), .store_clear_load(Control_signals[3:2]), .Output(R1_output));
  storeclearloadcircuit R2 (
    .\input (demultiplexer_1_out_2), .clk(CLK), .store_clear_load(Control_signals[5:4]), .Output(R2_output));
  storeclearloadcircuit R3 (
    .\input (demultiplexer_1_out_3), .clk(CLK), .store_clear_load(Control_signals[7:6]), .Output(R3_output));
  Multiplexer #(.Bits(4), .Selector_Bits(2)) multiplexer_1 (
    .sel(ReadRegister_1), .in_0(R0_output), .in_1(R1_output), .in_2(R2_output), .in_3(R3_output),
    .out(ReadData_1));
  Multiplexer #(.Selector_Bits(2), .Bits(4)) multiplexer_2 (
    .sel(ReadRegister_2), .in_0(R0_output), .in_1(R1_output), .in_2(R2_output), .in_3(R3_output),
    .out(ReadData_2));
endmodule
