// Digital circuit one bit full adder.dig as structural Verilog
module one_bit_full_adder (
  input  A,
  input  B,
  input  C,
  output Sum,
  output Carry
);

  wire and_1_out, and_2_out, xor_1_out;

  xor xor_1 (xor_1_out, A, B);
  and and_1 (and_1_out, A, B);
  and and_2 (and_2_out, xor_1_out, C);
  xor xor_2 (Sum, xor_1_out, C);
  xor xor_3 (Carry, and_2_out, and_1_out);
endmodule
