// Digital circuit programcounter.dig as structural Verilog
module programcounter (
  input  [3:0] \input ,
  input  clk,
  input  [1:0] store_clear_load_increment,
  input  [3:0] Increment,
  output [3:0] Output
);

  wire [3:0] add_1_s, multiplexer_1_out;

  Add #(.Bits(4)) add_1 (.a(Output), .b(Increment), .c_i(1'b0), .s(add_1_s));  // open: c_o
  Multiplexer #(.Selector_Bits(2), .Bits(4)) multiplexer_1 (
    .sel(store_clear_load_increment), .in_0(4'b0000), .in_1(\input ), .in_2(Output), .in_3(add_1_s),
    .out(multiplexer_1_out));
  D_FF d_ff_1 (.D(multiplexer_1_out[3]), .C(clk), .Q(Output[3]));  // open: nQ
  D_FF d_ff_2 (.D(multiplexer_1_out[2]), .C(clk), .Q(Output[2]));  // open: nQ
  D_FF d_ff_3 (.D(multiplexer_1_out[1]), .C(clk), .Q(Output[1]));  // open: nQ
  D_FF d_ff_4 (.D(multiplexer_1_out[0]), .C(clk), .Q(Output[0]));  // open: nQ

  // Notes on the sheet:
  //   store_clear_load_increment: 0 -> clear
  //   1-> store input
  //   2-> Load
  //   3 -> increment
  //   Increment: default 1
endmodule
