// Digital circuit storeclearloadcircuit.dig as structural Verilog
module storeclearloadcircuit (
  input  [3:0] \input ,
  input  clk,
  input  [1:0] store_clear_load,
  output [3:0] Output
);

  wire [3:0] multiplexer_1_out;

  Multiplexer #(.Bits(4), .Selector_Bits(2)) multiplexer_1 (
    .sel(store_clear_load), .in_0(4'b0000), .in_1(\input ), .in_2(Output), .in_3(4'b1111),
    .out(multiplexer_1_out));
  D_FF d_ff_1 (.D(multiplexer_1_out[3]), .C(clk), .Q(Output[3]));  // open: nQ
  D_FF d_ff_2 (.D(multiplexer_1_out[2]), .C(clk), .Q(Output[2]));  // open: nQ
  D_FF d_ff_3 (.D(multiplexer_1_out[1]), .C(clk), .Q(Output[1]));  // open: nQ
  D_FF d_ff_4 (.D(multiplexer_1_out[0]), .C(clk), .Q(Output[0]));  // open: nQ

  // Notes on the sheet:
  //   store_clear_load: 0 -> clear
  //   1-> store input
  //   2-> Load
  //   3 -> set F
endmodule
